// Digital circuit 1bit_full_adder_sana.dig as structural Verilog
module _1bit_full_adder_sana (
  input  A,
  input  B,
  input  Cin,
  output Sum,
  output Cout
);

  wire and_1_out, and_2_out, and_3_out, and_4_out, and_5_out, and_6_out, and_7_out, not_1_out, not_2_out,
       not_3_out, not_4_out, not_5_out, not_6_out;

  not not_1 (not_1_out, B);
  not not_2 (not_2_out, Cin);
  and and_1 (and_1_out, A, not_1_out, not_2_out);
  not not_3 (not_3_out, A);
  not not_4 (not_4_out, B);
  not not_5 (not_5_out, Cin);
  not not_6 (not_6_out, A);
  and and_2 (and_2_out, not_3_out, not_4_out, Cin);
  and and_3 (and_3_out, not_6_out, B, not_5_out);
  and and_4 (and_4_out, A, B, Cin);
  and and_5 (and_5_out, A, B);
  and and_6 (and_6_out, A, Cin);
  and and_7 (and_7_out, Cin, B);
  or or_1 (Sum, and_1_out, and_3_out, and_2_out, and_4_out);
  or or_2 (Cout, and_5_out, and_6_out, and_7_out);
endmodule
