// Digital circuit 4bit_ALU_Sana.dig as structural Verilog
module _4bit_ALU_Sana (
  input  [3:0] A,
  input  [3:0] B,
  input  [3:0] Control,
  input  Cin,
  input  [3:0] in_7,
  input  [3:0] in_10,
  input  [3:0] in_11,
  output [3:0] Output,
  output Zero_flag,
  output [3:0] SLT,
  output Cout
);

  wire _4bit_full_adder_sana_1_cout;
  wire [3:0] _4bit_full_adder_sana_1_sum, _4bit_subtractor_sana_1_subtraction, and_1_out, and_2_out,
       not_1_out, or_1_out, xor_1_out;
  wire [3:1] undriven, undriven_2;

  _4bit_full_Adder_sana _4bit_full_adder_sana_1 (
    .A(A), .B(B), .Cin(Cin), .Sum(_4bit_full_adder_sana_1_sum), .Cout(_4bit_full_adder_sana_1_cout));
  _4bit_subtractor_sana _4bit_subtractor_sana_1 (
    .A(A), .B(B), .C(_4bit_full_adder_sana_1_cout), .Subtraction(_4bit_subtractor_sana_1_subtraction),
    .Cout(Cout));
  assign and_1_out = A & B;  // And and_1, 4 bits wide
  assign or_1_out = A | B;  // Or or_1, 4 bits wide
  assign xor_1_out = A ^ B;  // XOr xor_1, 4 bits wide
  assign and_2_out = {undriven_2, Control[0]} & {undriven, Control[1]};  // And and_2, 4 bits wide
  Multiplexer #(.Bits(4), .Selector_Bits(3)) multiplexer_1 (
    .sel(Control[2:0]), .in_0(_4bit_full_adder_sana_1_sum), .in_1(_4bit_subtractor_sana_1_subtraction),
    .in_2(in_10), .in_3(in_11), .in_4(in_7), .in_5(and_1_out), .in_6(or_1_out), .in_7(xor_1_out),
    .out({{2{Output[3]}}, Output[1:0]}));
  not not_1 (not_1_out[0], Control[2]);
  assign SLT = and_2_out & not_1_out;  // And and_3, 4 bits wide
  nor nor_1 (Zero_flag, Output[0], Output[1], Output[3], Output[3]);
  // Pins of 3 and 4 bits meet at Control
  // Pins of 1 and 4 bits meet at {undriven_2, Control[0]}
  // Pins of 1 and 4 bits meet at {undriven, Control[1]}
  // Pins of 1 and 4 bits meet at not_1_out

  assign Output[2] = Output[3];
endmodule
