// Digital circuit 4bit_full_Adder_sana.dig as structural Verilog
module _4bit_full_Adder_sana (
  input  [3:0] A,
  input  [3:0] B,
  input  Cin,
  output [3:0] Sum,
  output Cout
);

  wire _1bit_full_adder_sana_1_cout, _1bit_full_adder_sana_2_cout, _1bit_full_adder_sana_3_cout;

  _1bit_full_adder_sana _1bit_full_adder_sana_1 (
    .A(A[0]), .B(A[1]), .Cin(Cin), .Sum(Sum[0]), .Cout(_1bit_full_adder_sana_1_cout));
  _1bit_full_adder_sana _1bit_full_adder_sana_2 (
    .A(A[1]), .B(B[1]), .Cin(_1bit_full_adder_sana_1_cout), .Sum(Sum[1]), .Cout(_1bit_full_adder_sana_2_cout));
  _1bit_full_adder_sana _1bit_full_adder_sana_3 (
    .A(A[2]), .B(B[2]), .Cin(_1bit_full_adder_sana_2_cout), .Sum(Sum[2]), .Cout(_1bit_full_adder_sana_3_cout));
  _1bit_full_adder_sana _1bit_full_adder_sana_4 (
    .A(A[3]), .B(B[3]), .Cin(_1bit_full_adder_sana_3_cout), .Sum(Sum[3]), .Cout(Cout));

  assign B[0] = A[1];
endmodule
