// Digital circuit 4bit_subtractor_sana.dig as structural Verilog
module _4bit_subtractor_sana (
  input  [3:0] A,
  input  [3:0] B,
  input  C,
  output [3:0] Subtraction,
  output Cout
);

  wire _1bit_full_adder_sana_1_cout, _1bit_full_adder_sana_2_cout, _1bit_full_adder_sana_3_cout, not_1_out,
       not_2_out, not_3_out, not_4_out;

  not not_1 (not_1_out, B[0]);
  not not_2 (not_2_out, B[1]);
  not not_3 (not_3_out, B[2]);
  not not_4 (not_4_out, B[3]);
  _1bit_full_adder_sana _1bit_full_adder_sana_1 (
    .A(A[0]), .B(not_1_out), .Cin(C), .Sum(Subtraction[0]), .Cout(_1bit_full_adder_sana_1_cout));
  _1bit_full_adder_sana _1bit_full_adder_sana_2 (
    .A(A[1]), .B(not_2_out), .Cin(_1bit_full_adder_sana_1_cout), .Sum(Subtraction[1]),
    .Cout(_1bit_full_adder_sana_2_cout));
  _1bit_full_adder_sana _1bit_full_adder_sana_3 (
    .A(A[2]), .B(not_3_out), .Cin(_1bit_full_adder_sana_2_cout), .Sum(Subtraction[2]),
    .Cout(_1bit_full_adder_sana_3_cout));
  _1bit_full_adder_sana _1bit_full_adder_sana_4 (
    .A(A[3]), .B(not_4_out), .Cin(_1bit_full_adder_sana_3_cout), .Sum(Subtraction[3]), .Cout(Cout));
endmodule
